# Fritzing sketch Untitled Sketch (saved by Fritzing 0.9.3b)
breadboards: 1

parts:
  R2 = PHOTOCELL [package=photocell-kit]
  LED1 = LEDs [package=led10mm]
  LED4 = smd LED [color="Red (633nm)" package="0805 [SMD]"]
  LED5 = smd LED [color="Green (555nm)" package="0805 [SMD]"]
  R4 = Resistor [tolerance=±5% resistance=220 package=THT]
  Componente1 = Arduino Uno (Rev3)
  J1 = Basic Servo
  R5 = Resistor [tolerance=±5% resistance=220 package=THT]
  R6 = Resistor [tolerance=±5% resistance=220 package=THT]

nets:
  N1: R2.P$1, R4.Pin_1, Componente1.A4/SDA
  5V: R2.P$2, Componente1.5V, J1.vcc
  N2: LED1.C, Componente1.D12/MISO
  GND: LED1.A, LED4.cathode, LED5.cathode, R4.Pin_0, Componente1.GND, J1.gnd
  N3: LED4.anode, R6.Pin_1
  N4: LED5.anode, R5.Pin_1
  N5: Componente1.D8, R5.Pin_0
  N6: Componente1.D3_PWM, J1.pulse
  N7: Componente1.D7, R6.Pin_0

notes:
  Arduino UNO representando um Arduino da familia MKR
  LED representando laser
  Servo representando porta
